// Logisim project 1-bit_ALU.circ as structural Verilog: 2 circuits, main circuit main
module main (
  input  Carry_In,
  input  INVA,
  input  A,
  input  ENA,
  input  B,
  input  ENB,
  input  F0,
  input  F1,
  output out_9,
  output out_10
);

  wire and_1_out, and_2_out, and_3_out, and_4_out, and_5_out, and_6_out, and_7_out, and_8_out, and_9_out,
       and_10_out, and_11_out, and_12_out, and_13_out, not_1_out, not_2_out, not_3_out, not_4_out, not_5_out,
       or_1_out, xor_1_out, xor_2_out, xor_3_out;

  and and_1 (and_1_out, A, ENA);
  and and_2 (and_2_out, B, ENB);
  not not_1 (not_1_out, F0);
  not not_2 (not_2_out, F1);
  not not_3 (not_3_out, F0);
  not not_4 (not_4_out, F1);
  xor xor_1 (xor_1_out, INVA, and_1_out);
  not not_5 (not_5_out, and_2_out);
  and and_3 (and_3_out, not_1_out, not_2_out);
  and and_4 (and_4_out, not_3_out, F1);
  and and_5 (and_5_out, F0, not_4_out);
  and and_6 (and_6_out, F0, F1);
  and and_7 (and_7_out, xor_1_out, and_2_out);
  or or_1 (or_1_out, xor_1_out, and_2_out);
  and and_8 (and_8_out, and_7_out, and_3_out);
  and and_9 (and_9_out, or_1_out, and_4_out);
  and and_10 (and_10_out, not_5_out, and_5_out);
  and and_11 (and_11_out, and_6_out, xor_1_out, and_2_out);
  xor xor_2 (xor_2_out, and_2_out, xor_1_out);
  and and_12 (and_12_out, and_6_out, xor_2_out, Carry_In);
  or or_2 (out_10, and_11_out, and_12_out);
  xor xor_3 (xor_3_out, Carry_In, xor_2_out);
  and and_13 (and_13_out, xor_3_out, and_6_out);
  or or_3 (out_9, and_8_out, and_9_out, and_10_out, and_13_out);
endmodule

module _1_Bit_Rechenwerk (
  input  Carry_In,
  input  INVA,
  input  A,
  input  ENA,
  input  B,
  input  ENB,
  input  F0,
  input  F1,
  output out_9,
  output out_10
);

  wire and_1_out, and_2_out, and_3_out, and_4_out, and_5_out, and_6_out, and_7_out, and_8_out, and_9_out,
       and_10_out, and_11_out, and_12_out, and_13_out, not_1_out, not_2_out, not_3_out, not_4_out, not_5_out,
       or_1_out, xor_1_out, xor_2_out, xor_3_out;

  and and_1 (and_1_out, A, ENA);
  and and_2 (and_2_out, B, ENB);
  not not_1 (not_1_out, F0);
  not not_2 (not_2_out, F1);
  not not_3 (not_3_out, F0);
  not not_4 (not_4_out, F1);
  xor xor_1 (xor_1_out, INVA, and_1_out);
  not not_5 (not_5_out, and_2_out);
  and and_3 (and_3_out, not_1_out, not_2_out);
  and and_4 (and_4_out, not_3_out, F1);
  and and_5 (and_5_out, F0, not_4_out);
  and and_6 (and_6_out, F0, F1);
  and and_7 (and_7_out, xor_1_out, and_2_out);
  or or_1 (or_1_out, xor_1_out, and_2_out);
  and and_8 (and_8_out, and_7_out, and_3_out);
  and and_9 (and_9_out, or_1_out, and_4_out);
  and and_10 (and_10_out, not_5_out, and_5_out);
  and and_11 (and_11_out, and_6_out, xor_1_out, and_2_out);
  xor xor_2 (xor_2_out, and_2_out, xor_1_out);
  and and_12 (and_12_out, and_6_out, xor_2_out, Carry_In);
  or or_2 (out_10, and_11_out, and_12_out);
  xor xor_3 (xor_3_out, Carry_In, xor_2_out);
  and and_13 (and_13_out, xor_3_out, and_6_out);
  or or_3 (out_9, and_8_out, and_9_out, and_10_out, and_13_out);
endmodule
