// Logisim project animal_training.circ as structural Verilog: 1 circuit, main circuit main
module main (
  input  A_Sitz,
  input  B_Sitz,
  input  C_Sitz
);

  wire A_Nase_out, and_1_out, and_2_out, and_3_out, and_4_out, and_5_out, B_Nase_out, buffer_1_out,
       C_Nase_out, D_Flip_Flop_2_q, D_Flip_Flop_3_q, D_Flip_Flop_q, not_1_out, or_1_out, or_2_out, or_3_out,
       Reset_out;

  Button A_Nase (.out(A_Nase_out));
  Button B_Nase (.out(B_Nase_out));
  Button C_Nase (.out(C_Nase_out));
  LED Belohnung (.in(D_Flip_Flop_3_q));
  Button Reset (.out(Reset_out));
  buf buffer_1 (buffer_1_out, Reset_out);
  not not_1 (not_1_out, Reset_out);
  or or_1 (or_1_out, buffer_1_out, A_Nase_out);
  or or_2 (or_2_out, buffer_1_out, B_Nase_out);
  or or_3 (or_3_out, buffer_1_out, C_Nase_out);
  and and_1 (and_1_out, not_1_out, A_Sitz);
  and and_2 (and_2_out, not_1_out, B_Sitz);
  and and_3 (and_3_out, not_1_out, C_Sitz);
  D_Flip_Flop D_Flip_Flop (.clk(or_1_out), .D(and_1_out), .Q(D_Flip_Flop_q));  // open: Qn, preset, en, reset
  and and_4 (and_4_out, D_Flip_Flop_q, or_2_out);
  D_Flip_Flop D_Flip_Flop_2 (.clk(and_4_out), .D(and_2_out), .Q(D_Flip_Flop_2_q));  // open: Qn, preset, en, reset
  and and_5 (and_5_out, D_Flip_Flop_2_q, or_3_out);
  D_Flip_Flop D_Flip_Flop_3 (.clk(and_5_out), .D(and_3_out), .Q(D_Flip_Flop_3_q));  // open: Qn, preset, en, reset
endmodule
