// Logisim project binary_to_decimal_7_segment_output.circ as structural Verilog: 1 circuit, main circuit main
module main (
  input  in_1,
  input  in_2,
  input  in_3,
  input  in_4
);

  wire and_1_out, and_2_out, and_3_out, and_4_out, and_5_out, not_1_out, not_2_out, not_3_out, not_4_out,
       not_5_out, not_6_out, not_7_out, not_8_out, not_9_out, not_10_out, not_11_out, not_12_out, not_13_out,
       not_14_out, not_15_out, not_16_out, not_17_out, not_18_out, not_19_out, or_1_out, or_2_out, or_3_out,
       or_4_out, or_5_out, or_6_out, or_7_out, or_8_out, or_9_out, or_10_out, or_11_out, or_12_out,
       or_13_out, or_14_out, or_15_out, or_16_out, or_17_out, or_18_out, or_19_out, or_20_out, or_21_out,
       or_22_out, or_23_out, or_24_out, or_25_out;

  not not_1 (not_1_out, or_1_out);
  not not_2 (not_2_out, or_2_out);
  not not_3 (not_3_out, or_5_out);
  not not_4 (not_4_out, or_8_out);
  not not_5 (not_5_out, or_10_out);
  or or_1 (or_1_out, in_1, in_2, in_3, in_4);
  not not_6 (not_6_out, or_13_out);
  not not_7 (not_7_out, or_16_out);
  not not_8 (not_8_out, or_19_out);
  not not_9 (not_9_out, or_22_out);
  not not_10 (not_10_out, or_24_out);
  or or_2 (or_2_out, or_3_out, not_11_out);
  not not_11 (not_11_out, and_1_out);
  and and_1 (and_1_out, in_1, in_4);
  or or_3 (or_3_out, in_2, in_3);
  or or_4 (or_4_out, not_7_out, not_6_out, not_5_out, not_3_out, not_2_out, not_1_out);
  or or_5 (or_5_out, or_6_out, not_12_out);
  not not_12 (not_12_out, in_1);
  or or_6 (or_6_out, in_2, in_3, in_4);
  or or_7 (or_7_out, not_9_out, not_8_out, not_7_out, not_6_out, not_5_out, not_3_out, not_2_out);
  or or_8 (or_8_out, not_13_out, in_1);
  not not_13 (not_13_out, and_2_out);
  and and_2 (and_2_out, in_2, in_3, in_4);
  or or_9 (or_9_out, not_9_out, not_5_out, not_3_out, not_1_out);
  or or_10 (or_10_out, not_14_out, or_11_out);
  not not_14 (not_14_out, and_3_out);
  or or_11 (or_11_out, in_1, in_4);
  and and_3 (and_3_out, in_2, in_3);
  _7_Segment_Display u_7_segment_display_1 (
    .g(or_7_out), .f(or_4_out), .a(or_21_out), .b(or_18_out), .e(or_9_out), .d(or_12_out), .c(or_15_out));  // open: dp
  or or_12 (or_12_out, not_9_out, not_8_out, not_6_out, not_5_out, not_3_out, not_2_out, not_1_out);
  or or_13 (or_13_out, not_15_out, or_14_out);
  not not_15 (not_15_out, and_4_out);
  and and_4 (and_4_out, in_2, in_4);
  or or_14 (or_14_out, in_1, in_3);
  or or_15 (or_15_out, not_10_out, not_8_out, not_7_out, not_6_out, not_5_out, not_4_out, not_3_out, not_2_out, not_1_out);
  or or_16 (or_16_out, or_17_out, not_16_out);
  not not_16 (not_16_out, in_2);
  or or_17 (or_17_out, in_1, in_3, in_4);
  or or_18 (or_18_out, not_10_out, not_9_out, not_8_out, not_7_out, not_4_out, not_3_out, not_2_out, not_1_out);
  or or_19 (or_19_out, or_20_out, not_17_out);
  not not_17 (not_17_out, and_5_out);
  or or_20 (or_20_out, in_1, in_2);
  and and_5 (and_5_out, in_3, in_4);
  or or_21 (or_21_out, not_1_out, not_2_out, not_3_out, not_4_out, not_5_out, not_6_out, not_8_out, not_9_out);
  or or_22 (or_22_out, or_23_out, not_18_out);
  not not_18 (not_18_out, in_3);
  or or_23 (or_23_out, in_1, in_2, in_4);
  or or_24 (or_24_out, or_25_out, not_19_out);
  not not_19 (not_19_out, in_4);
  or or_25 (or_25_out, in_1, in_2, in_3);
endmodule
