// Logisim project hamming_distance.circ as structural Verilog: 3 circuits, main circuit main
module main (
  input  a0,
  input  a1,
  input  a2,
  input  a3,
  input  b0,
  input  b1,
  input  b2,
  input  b3,
  output [2:0] Hamming_Distanz
);

  wire xor_1_out, xor_2_out, xor_3_out, xor_4_out;

  xor xor_1 (xor_1_out, a0, b0);
  xor xor_2 (xor_2_out, a1, b1);
  xor xor_3 (xor_3_out, a2, b2);
  xor xor_4 (xor_4_out, a3, b3);
  BitAdder #(.width(1)) bitadder_1 (
    .in0(xor_1_out), .in1(xor_2_out), .in2(xor_3_out), .in3(xor_4_out), .out(Hamming_Distanz));
endmodule

module _11_3 (
  input  a0,
  input  a1,
  input  a2,
  input  a3,
  input  b0,
  input  b1,
  input  b2,
  input  b3,
  output out_9,
  output out_10,
  output out_11,
  output out_12,
  output out_13
);

  wire adder_1_cout, adder_1_out, adder_2_cout, and_1_out, and_2_out, and_4_out, or_1_out, undriven,
       undriven_2, xor_1_out, xor_2_out, xor_3_out, xor_4_out;

  xor xor_1 (xor_1_out, a0, b0);
  xor xor_2 (xor_2_out, a1, b1);
  xor xor_3 (xor_3_out, a2, b2);
  xor xor_4 (xor_4_out, a3, b3);
  and and_1 (and_1_out, xor_2_out, xor_1_out);
  and and_2 (and_2_out, xor_4_out, xor_3_out);
  and and_3 (out_9, xor_1_out, xor_2_out, xor_3_out, xor_4_out);
  xor xor_5 (out_10, xor_1_out, xor_2_out);
  xor xor_6 (out_11, xor_3_out, xor_4_out);
  or or_1 (or_1_out, and_2_out, and_4_out);
  and and_4 (and_4_out, out_11, and_1_out);
  Adder #(.width(1)) adder_1 (.out(adder_1_out), .cout(adder_1_cout));  // open: a, b, cin
  Adder #(.width(1)) adder_2 (.a(undriven), .b(undriven_2), .out(out_13), .cin(adder_1_cout), .cout(adder_2_cout));
  or or_2 (out_12, adder_1_out, adder_2_cout);
endmodule

module _11_3_2 (
  input  a0,
  input  a1,
  input  a2,
  input  a3,
  input  b0,
  input  b1,
  input  b2,
  input  b3,
  input  in_9,
  output out_10,
  output out_11,
  output out_12,
  output out_13,
  output out_14,
  output out_15,
  output out_16,
  output out_17
);

  wire d_ff_1_qn, d_ff_2_qn, d_ff_3_qn, d_ff_4_qn, or_1_out, xor_1_out, xor_2_out, xor_3_out, xor_4_out;

  xor xor_1 (xor_1_out, a0, b0);
  xor xor_2 (xor_2_out, a1, b1);
  xor xor_3 (xor_3_out, a2, b2);
  xor xor_4 (xor_4_out, a3, b3);
  T_Flip_Flop t_ff_1 (.clk(or_1_out), .T(xor_1_out), .Q(out_10));  // open: Qn, preset, reset, en
  D_Flip_Flop d_ff_1 (.clk(in_9), .D(d_ff_1_qn), .Q(out_14), .Qn(d_ff_1_qn));  // open: preset, en, reset
  or or_1 (or_1_out, xor_1_out, xor_2_out, xor_3_out, xor_4_out);
  T_Flip_Flop t_ff_2 (.clk(out_10), .T(xor_2_out), .Q(out_11));  // open: Qn, preset, reset, en
  D_Flip_Flop d_ff_2 (.clk(d_ff_1_qn), .D(d_ff_2_qn), .Q(out_15), .Qn(d_ff_2_qn));  // open: preset, en, reset
  D_Flip_Flop d_ff_3 (.clk(d_ff_2_qn), .D(d_ff_3_qn), .Q(out_16), .Qn(d_ff_3_qn));  // open: preset, en, reset
  T_Flip_Flop t_ff_3 (.clk(out_11), .T(xor_3_out), .Q(out_12));  // open: Qn, preset, reset, en
  T_Flip_Flop t_ff_4 (.clk(out_12), .T(xor_4_out), .Q(out_13));  // open: Qn, preset, reset, en
  D_Flip_Flop d_ff_4 (.clk(d_ff_3_qn), .D(d_ff_4_qn), .Q(out_17), .Qn(d_ff_4_qn));  // open: preset, en, reset
endmodule
